# Fritzing sketch pracaDyplomowa (saved by Fritzing 0.9.2b)
breadboards: 1

parts:
  Part1 = Arduino Uno (Rev3)
  LCD1 = LCD screen
  S1 = Momentary Switch [package=ksa_sealed_tac_switch]
  S2 = Momentary Switch [package=ksa_sealed_tac_switch]
  T1 = LM35 Temperature Sensor [package="TO92 [THT]"]
  T2 = LM35 Temperature Sensor [package="TO92 [THT]"]
  Power_plug1 = Power plug
  M1 = DC Motor
  R1 = Trimmer Potentiometer [maximum_resistance=10kΩ package=THT]
  KY-1 = Keyes Relay [package=THT]

nets:
  N1: Part1.A0, T1.Vout
  N2: Part1.A1, T2.Vout
  N3: Part1.D8, LCD1.DB5
  N4: Part1.D10_PWM/SS, LCD1.DB4
  N5: Part1.D11_PWM/MOSI, LCD1.E
  N6: Part1.D12/MISO, LCD1.RS
  N7: Part1.D2, S2.2
  N8: Part1.D3_PWM, S1.2
  N9: Part1.D4, KY-1.signal
  N10: Part1.D6_PWM, LCD1.DB7
  N11: Part1.D7, LCD1.DB6
  5V: Part1.5V, LCD1.VDD, LCD1.LED+, T1.+Vs, T2.+Vs, R1.leg1, KY-1.power
  GND: Part1.GND, LCD1.VSS, LCD1.R/W, LCD1.LED-, S1.3, S2.3, T1.GND, T2.GND, R1.leg2, KY-1.ground
  N12: LCD1.V0, R1.wiper
  N13: Power_plug1.VCC, KY-1.C
  N14: Power_plug1.GND, M1.pin_2
  N15: M1.pin_1, KY-1.NO

custom parts:
  Keyes Relay: The Keyes 5V relay module is suitable for SCM development, home appliance control. It uses a 5V~12V TIL control signal which can control DC / AC signal.
